// Logisim project d-flip-flop.circ as structural Verilog: 1 circuit, main circuit main
module main (
  input  D,
  output Q,
  output Q_prime
);

  wire Clock_out, nand_1_out, nand_2_out;

  Clock Clock (.out(Clock_out));
  nand nand_1 (nand_1_out, D, Clock_out);
  nand nand_2 (nand_2_out, ~D, Clock_out);  // NAND_Gate
  nand nand_3 (Q, nand_1_out, Q_prime);
  nand nand_4 (Q_prime, Q, nand_2_out);
endmodule
