// Logisim project multiplexador-4x1.circ as structural Verilog: 1 circuit, main circuit main
module main (
  input  S0,
  input  S1,
  input  I1,
  input  I2,
  input  I3,
  input  I4,
  output O
);

  wire and_1_out, and_2_out, and_3_out, and_4_out;

  and and_1 (and_1_out, I1, ~S1, ~S0);  // AND_Gate
  and and_2 (and_2_out, I2, S1, ~S0);  // AND_Gate
  and and_3 (and_3_out, I3, ~S1, S0);  // AND_Gate
  and and_4 (and_4_out, I4, S1, S0);
  or or_1 (O, and_1_out, and_2_out, and_3_out, and_4_out);
endmodule
