// Logisim project adder-4.circ as structural Verilog: 2 circuits, main circuit main
module main (
  input  [7:0] in_1,
  output [7:0] out_2
);

  wire adder_1_out_5, adder_2_out_5, adder_3_out_5, adder_4_out_5, adder_5_out_5, adder_6_out_5,
       adder_7_out_5, not_1_out;

  not not_1 (not_1_out, 1'b0);
  adder adder_1 (.in_1(in_1[0]), .in_2(1'b0), .in_3(1'b0), .out_4(out_2[0]), .out_5(adder_1_out_5));
  adder adder_2 (.in_1(in_1[1]), .in_2(1'b0), .in_3(adder_1_out_5), .out_4(out_2[1]), .out_5(adder_2_out_5));
  adder adder_3 (.in_1(in_1[2]), .in_2(not_1_out), .in_3(adder_2_out_5), .out_4(out_2[2]), .out_5(adder_3_out_5));
  adder adder_4 (.in_1(in_1[3]), .in_2(1'b0), .in_3(adder_3_out_5), .out_4(out_2[3]), .out_5(adder_4_out_5));
  adder adder_5 (.in_1(in_1[4]), .in_2(1'b0), .in_3(adder_4_out_5), .out_4(out_2[4]), .out_5(adder_5_out_5));
  adder adder_6 (.in_1(in_1[5]), .in_2(1'b0), .in_3(adder_5_out_5), .out_4(out_2[5]), .out_5(adder_6_out_5));
  adder adder_7 (.in_1(in_1[6]), .in_2(1'b0), .in_3(adder_6_out_5), .out_4(out_2[6]), .out_5(adder_7_out_5));
  adder adder_8 (.in_1(in_1[7]), .in_2(1'b0), .in_3(adder_7_out_5), .out_4(out_2[7]));  // open: out_5
endmodule

module adder (
  input  in_1,
  input  in_2,
  input  in_3,
  output out_4,
  output out_5
);

  wire and_1_out, and_2_out, xor_1_out;

  xor xor_1 (xor_1_out, in_1, in_2);
  and and_1 (and_1_out, in_3, xor_1_out);
  and and_2 (and_2_out, in_2, in_1);
  xor xor_2 (out_4, xor_1_out, in_3);
  or or_1 (out_5, and_1_out, and_2_out);
endmodule
