// Logisim project banco-de-registradores.circ as structural Verilog: 8 circuits, main circuit main
module main (
  input  [7:0] WD3,
  input  [2:0] A1,
  input  [2:0] A3,
  input  WE3,
  input  [2:0] A2,
  input  Reset,
  output [7:0] RD1,
  output [7:0] RD2
);

  wire clock_1_out, demultiplexer_1x8_1_out_3, demultiplexer_1x8_1_out_4, demultiplexer_1x8_1_out_5,
       demultiplexer_1x8_1_out_6, demultiplexer_1x8_1_out_7, demultiplexer_1x8_1_out_8,
       demultiplexer_1x8_1_out_9, demultiplexer_1x8_1_out_10;
  wire [7:0] register_1_output, register_2_output, register_3_output, register_4_output, register_5_output,
       register_6_output, register_7_output, register_8_output;

  Clock clock_1 (.out(clock_1_out));
  demultiplexer_1x8 demultiplexer_1x8_1 (
    .in_1(A3), .in_2(WE3), .out_3(demultiplexer_1x8_1_out_3), .out_4(demultiplexer_1x8_1_out_4),
    .out_5(demultiplexer_1x8_1_out_5), .out_6(demultiplexer_1x8_1_out_6), .out_7(demultiplexer_1x8_1_out_7),
    .out_8(demultiplexer_1x8_1_out_8), .out_9(demultiplexer_1x8_1_out_9), .out_10(demultiplexer_1x8_1_out_10));
  register register_1 (
    .Input(WD3), .Reset(Reset), .WE(demultiplexer_1x8_1_out_3), .Clock(clock_1_out),
    .Output(register_1_output));
  register register_2 (
    .Input(WD3), .Reset(Reset), .WE(demultiplexer_1x8_1_out_4), .Clock(clock_1_out),
    .Output(register_2_output));
  register register_3 (
    .Input(WD3), .Reset(Reset), .WE(demultiplexer_1x8_1_out_5), .Clock(clock_1_out),
    .Output(register_3_output));
  register register_4 (
    .Input(WD3), .Reset(Reset), .WE(demultiplexer_1x8_1_out_6), .Clock(clock_1_out),
    .Output(register_4_output));
  register register_5 (
    .Input(WD3), .Reset(Reset), .WE(demultiplexer_1x8_1_out_7), .Clock(clock_1_out),
    .Output(register_5_output));
  register register_6 (
    .Input(WD3), .Reset(Reset), .WE(demultiplexer_1x8_1_out_8), .Clock(clock_1_out),
    .Output(register_6_output));
  register register_7 (
    .Input(WD3), .Reset(Reset), .WE(demultiplexer_1x8_1_out_9), .Clock(clock_1_out),
    .Output(register_7_output));
  register register_8 (
    .Input(WD3), .Reset(Reset), .WE(demultiplexer_1x8_1_out_10), .Clock(clock_1_out),
    .Output(register_8_output));
  multiplexer_8x1_8bits multiplexer_8x1_8bits_1 (
    .in_2(register_1_output), .in_3(register_2_output), .in_4(register_3_output), .in_5(register_4_output),
    .in_6(register_5_output), .in_7(register_6_output), .in_8(register_7_output), .in_9(register_8_output),
    .in_1(A1), .out_10(RD1));
  multiplexer_8x1_8bits multiplexer_8x1_8bits_2 (
    .in_2(register_1_output), .in_3(register_2_output), .in_4(register_3_output), .in_5(register_4_output),
    .in_6(register_5_output), .in_7(register_6_output), .in_8(register_7_output), .in_9(register_8_output),
    .in_1(A2), .out_10(RD2));
endmodule

module d_flip_flop (
  input  Reset,
  input  D,
  input  Clock,
  input  Set,
  output Q,
  output nQ
);

  wire and_1_out, and_2_out;

  and and_1 (and_1_out, ~D, Clock);  // AND_Gate
  and and_2 (and_2_out, D, Clock);
  nor nor_1 (Q, Reset, and_1_out, nQ);
  nor nor_2 (nQ, Q, and_2_out, Set);
endmodule

module register (
  input  [7:0] Input,
  input  Reset,
  input  WE,
  input  Clock,
  output [7:0] Output
);

  wire and_1_out;

  and and_1 (and_1_out, WE, Clock);
  d_flip_flop d_flip_flop_1 (.Reset(Reset), .D(Input[0]), .Clock(and_1_out), .Set(1'b0), .Q(Output[0]));  // open: nQ
  d_flip_flop d_flip_flop_2 (.Reset(Reset), .D(Input[1]), .Clock(and_1_out), .Set(1'b0), .Q(Output[1]));  // open: nQ
  d_flip_flop d_flip_flop_3 (.Reset(Reset), .D(Input[2]), .Clock(and_1_out), .Set(1'b0), .Q(Output[2]));  // open: nQ
  d_flip_flop d_flip_flop_4 (.Reset(Reset), .D(Input[3]), .Clock(and_1_out), .Set(1'b0), .Q(Output[3]));  // open: nQ
  d_flip_flop d_flip_flop_5 (.Reset(Reset), .D(Input[4]), .Clock(and_1_out), .Set(1'b0), .Q(Output[4]));  // open: nQ
  d_flip_flop d_flip_flop_6 (.Reset(Reset), .D(Input[5]), .Clock(and_1_out), .Set(1'b0), .Q(Output[5]));  // open: nQ
  d_flip_flop d_flip_flop_7 (.Reset(Reset), .D(Input[6]), .Clock(and_1_out), .Set(1'b0), .Q(Output[6]));  // open: nQ
  d_flip_flop d_flip_flop_8 (.Reset(Reset), .D(Input[7]), .Clock(and_1_out), .Set(1'b0), .Q(Output[7]));  // open: nQ
endmodule

module demultiplexer_1x8 (
  input  [2:0] in_1,
  input  in_2,
  output out_3,
  output out_4,
  output out_5,
  output out_6,
  output out_7,
  output out_8,
  output out_9,
  output out_10
);

  wire not_1_out, not_2_out, not_3_out;

  not not_1 (not_1_out, in_1[2]);
  not not_2 (not_2_out, in_1[0]);
  not not_3 (not_3_out, in_1[1]);
  and and_1 (out_3, in_2, not_2_out, not_3_out, not_1_out);
  and and_2 (out_4, in_2, in_1[0], not_3_out, not_1_out);
  and and_3 (out_5, in_2, not_2_out, in_1[1], not_1_out);
  and and_4 (out_6, in_2, in_1[0], in_1[1], not_1_out);
  and and_5 (out_7, in_2, not_2_out, not_3_out, in_1[2]);
  and and_6 (out_8, in_2, in_1[0], not_3_out, in_1[2]);
  and and_7 (out_9, in_2, not_2_out, in_1[1], in_1[2]);
  and and_8 (out_10, in_2, in_1[0], in_1[1], in_1[2]);
endmodule

module multiplexer_8x1 (
  input  [2:0] in_1,
  input  in_2,
  input  in_3,
  input  in_4,
  input  in_5,
  input  in_6,
  input  in_7,
  input  in_8,
  input  in_9,
  output out_10
);

  wire and_1_out, and_2_out, and_3_out, and_4_out, and_5_out, and_6_out, and_7_out, and_8_out, not_1_out,
       not_2_out, not_3_out;

  not not_1 (not_1_out, in_1[2]);
  not not_2 (not_2_out, in_1[0]);
  not not_3 (not_3_out, in_1[1]);
  and and_1 (and_1_out, in_2, not_2_out, not_3_out, not_1_out);
  and and_2 (and_2_out, in_3, in_1[0], not_3_out, not_1_out);
  and and_3 (and_3_out, in_4, not_2_out, in_1[1], not_1_out);
  and and_4 (and_4_out, in_5, in_1[0], in_1[1], not_1_out);
  and and_5 (and_5_out, in_6, not_2_out, not_3_out, in_1[2]);
  and and_6 (and_6_out, in_7, in_1[0], not_3_out, in_1[2]);
  and and_7 (and_7_out, in_8, not_2_out, in_1[1], in_1[2]);
  and and_8 (and_8_out, in_9, in_1[0], in_1[1], in_1[2]);
  or or_1 (out_10, and_1_out, and_2_out, and_3_out, and_4_out, and_5_out, and_6_out, and_7_out, and_8_out);
endmodule

module multiplexer_8x1_2bits (
  input  [2:0] in_1,
  input  [1:0] in_2,
  input  [1:0] in_3,
  input  [1:0] in_4,
  input  [1:0] in_5,
  input  [1:0] in_6,
  input  [1:0] in_7,
  input  [1:0] in_8,
  input  [1:0] in_9,
  output [1:0] out_10
);

  multiplexer_8x1 multiplexer_8x1_1 (
    .in_1(in_1), .in_2(in_2[0]), .in_3(in_3[0]), .in_4(in_4[0]), .in_5(in_5[0]), .in_6(in_6[0]),
    .in_7(in_7[0]), .in_8(in_8[0]), .in_9(in_9[0]), .out_10(out_10[0]));
  multiplexer_8x1 multiplexer_8x1_2 (
    .in_1(in_1), .in_2(in_2[1]), .in_3(in_3[1]), .in_4(in_4[1]), .in_5(in_5[1]), .in_6(in_6[1]),
    .in_7(in_7[1]), .in_8(in_8[1]), .in_9(in_9[1]), .out_10(out_10[1]));
endmodule

module multiplexer_8x1_4bits (
  input  [2:0] in_1,
  input  [3:0] in_2,
  input  [3:0] in_3,
  input  [3:0] in_4,
  input  [3:0] in_5,
  input  [3:0] in_6,
  input  [3:0] in_7,
  input  [3:0] in_8,
  input  [3:0] in_9,
  output [3:0] out_10
);

  multiplexer_8x1_2bits multiplexer_8x1_2bits_1 (
    .in_1(in_1), .in_2(in_2[1:0]), .in_3(in_3[1:0]), .in_4(in_4[1:0]), .in_5(in_5[1:0]), .in_6(in_6[1:0]),
    .in_7(in_7[1:0]), .in_8(in_8[1:0]), .in_9(in_9[1:0]), .out_10(out_10[1:0]));
  multiplexer_8x1_2bits multiplexer_8x1_2bits_2 (
    .in_1(in_1), .in_2(in_2[3:2]), .in_3(in_3[3:2]), .in_4(in_4[3:2]), .in_5(in_5[3:2]), .in_6(in_6[3:2]),
    .in_7(in_7[3:2]), .in_8(in_8[3:2]), .in_9(in_9[3:2]), .out_10(out_10[3:2]));
endmodule

module multiplexer_8x1_8bits (
  input  [2:0] in_1,
  input  [7:0] in_2,
  input  [7:0] in_3,
  input  [7:0] in_4,
  input  [7:0] in_5,
  input  [7:0] in_6,
  input  [7:0] in_7,
  input  [7:0] in_8,
  input  [7:0] in_9,
  output [7:0] out_10
);

  multiplexer_8x1_4bits multiplexer_8x1_4bits_1 (
    .in_1(in_1), .in_2(in_2[3:0]), .in_3(in_3[3:0]), .in_4(in_4[3:0]), .in_5(in_5[3:0]), .in_6(in_6[3:0]),
    .in_7(in_7[3:0]), .in_8(in_8[3:0]), .in_9(in_9[3:0]), .out_10(out_10[3:0]));
  multiplexer_8x1_4bits multiplexer_8x1_4bits_2 (
    .in_1(in_1), .in_2(in_2[7:4]), .in_3(in_3[7:4]), .in_4(in_4[7:4]), .in_5(in_5[7:4]), .in_6(in_6[7:4]),
    .in_7(in_7[7:4]), .in_8(in_8[7:4]), .in_9(in_9[7:4]), .out_10(out_10[7:4]));
endmodule
